# Fritzing sketch KAneda-JFG (saved by Fritzing 1.0.1rc)

parts:
  Acelerómetro_MPU-6050 = InvenSense MPU6050
  SG1 = Tower Pro SG90 servo [part_number=101246]
  IC1 = Rasberry Pi NIOR Camera [chip_label=IC package="DIP (Dual Inline) [THT]"]  # not connected
  Componente1 = PowerBoost 500 Charger
  U1 = Battery Holders [package=lipo-1100mAh]
  Raspberry_Pi1 = Raspberry Pi Zero
  GM15BY3 = Micromotor Stepper GM15BY 15mm
  U2 = L298 [package=multiwatt15]
  M1 = DC Motor [voltage_(max)=6V voltage_(min)=3V]
  VCC1 = Battery block 9V
  X1 = USB Connectors [package=usb-microb]

nets:
  3V3: Acelerómetro_MPU-6050.VCC, SG1.+5V, Raspberry_Pi1.3v3, Raspberry_Pi1.3V3
  GND: Acelerómetro_MPU-6050.GND, SG1.GND, Raspberry_Pi1.GND, U2.GND, VCC1.-
  N1: Acelerómetro_MPU-6050.SCL, Raspberry_Pi1.GPIO3
  N2: Acelerómetro_MPU-6050.SDA, Raspberry_Pi1.GPIO2
  N3: SG1.Signal, Raspberry_Pi1.GIPO9
  N4: Componente1.VBAT, U1.+
  GND_2: Componente1.GND, Componente1.USB, U1.-, X1.GND
  N5: Componente1.5.0V, X1.VBUS
  N6: Raspberry_Pi1.GIPO13, GM15BY3.C
  N7: Raspberry_Pi1.GIPO19, GM15BY3.B
  N8: Raspberry_Pi1.GIPO15, U2.IN2
  N9: Raspberry_Pi1.GIPO14, U2.IN1
  N10: Raspberry_Pi1.5V, GM15BY3.A, U2.VLS
  N11: Raspberry_Pi1.PWR_IN, X1.D+, X1.D-
  N12: U2.OUT1, M1.pin_2
  N13: U2.OUT2, M1.pin_1
  N14: U2.VS, VCC1.+

custom parts:
  Tower Pro SG90 servo: Original file by John De Cristofaro http://www.adafruit.com/products/1449 Adafruit Feedback Servo (Small) Edited by: e-radionica.com 28/9/2015
  Rasberry Pi NIOR Camera: Camera
  PowerBoost 500 Charger: The PowerBoost 500C is a little DC/DC boost converter module that can be powered by any 3.7V LiIon/LiPoly battery, and convert the battery output to 5.2V DC for running your 5V projects. At its heart is a TPS61090 boost converter from TI. This boost converter chip has some really nice extras such as low battery detection, 2A internal switch, synchronous conversion, excellent efficiency, and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
  Raspberry Pi Zero: The Raspberry Pi Zero is the latest single board computer to be released by the Raspberry Pi Foundation. It is the entry level model Raspberry Pi perfect for hobbyists, makers and industrial engineers looking to create solutions where small size and low power consumption are important. This is especially relevant for applications in the wearables space as well as up and coming applications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
  Micromotor Stepper GM15BY 15mm: Motor paso a paso de 5V ultra pequeño con reductora de 1:150.
